# Fritzing sketch hexbotBreadboard (saved by Fritzing 0.9.4)
breadboards: 1

parts:
  PWM1 = PCA9685 16x12-bit PWM Breakout
  PWM2 = PCA9685 16x12-bit PWM Breakout
  Part1 = Adafruit 128x64 OLED FeatherWing [part_number="Adafruit #4650"]
  LED1 = RGB LED - (4 legs) [package="5 mm [THT]"]
  LED3 = LED - 5mm [color="Red (633nm)" package="5 mm [THT]"]
  S1 = Round Pushbutton
  S2 = Round Pushbutton
  VCC1 = Battery
  U1 = LM2596 step down module

nets:
  N1: PWM1.no_name_yet#501, PWM1.no_name_yet#601, PWM1.no_name_yet#701, PWM2.no_name_yet#501, PWM2.no_name_yet#701, Part1.GND, LED3.anode, S2.leg0, VCC1.-, U1.IN-, U1.OUT-
  N2: PWM1.no_name_yet#503, PWM1.no_name_yet#603, PWM2.no_name_yet#503, Part1.SDA
  N3: PWM1.no_name_yet#504, PWM1.no_name_yet#604, PWM2.no_name_yet#504, Part1.SCL
  N4: PWM1.no_name_yet#505, PWM1.no_name_yet#605, PWM2.no_name_yet#505, Part1.3.3V
  N5: PWM1.no_name_yet#706, PWM2.no_name_yet#706, LED1.red_cathode, LED3.cathode, S1.leg1
  N6: Part1.!RESET, S2.leg1
  N7: Part1.12, LED1.blue_cathode
  N8: Part1.22, LED1.green_cathode
  N9: Part1.23, LED1.common_anode
  N10: S1.leg0, U1.OUT+
  N11: VCC1.+, U1.IN+

notes:
  [write your note here]

custom parts:
  Adafruit 128x64 OLED FeatherWing: A Feather board without ambition is a Feather board without FeatherWings! This is the FeatherWing 128x64 OLED: it adds a gorgeous 128x64 monochrome OLED plus 3 user buttons to any Feather main board. Using our Feather Stacking Headers or Feather Female Headers you can connect a FeatherWing on top of your Feather board and let the board take flight! These displays are small, only about 1.3"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
  LM2596 step down module: LM2596 DC-DC step down power supply module 3 A.
